# Fritzing sketch on,off (saved by Fritzing 0.9.4)
breadboards: 1

parts:
  Part1 = Arduino Ethernet Shield (Rev3)
  LED1 = LED - 5mm [color="Red (633nm)" package="5 mm [THT]"]

nets:
  N1: Part1.SPI/D13, LED1.cathode
  N2: Part1.GND, LED1.anode
